// Logisim project CIOTTO_GARCIA_C15.circ as structural Verilog: 1 circuit, main circuit main
module main (
);

  wire C5, C6, C7, C8, CCO, control_unit_1_p6, HAQ, HCO, HEM, HEtat, HRADM, HRI, inc_register_1_p11,
       inc_register_1_p14, not_1_out, not_2_out, RW, Sext, U0, U1, U2, U3, VAQ, VARG, VCO, VSM;
  wire [1:0] alu_1_p9, register_3_q;
  wire [15:0] controlled_buffer_4_out, inc_register_1_p9, inc_register_1_p10, inc_register_1_p12,
       inc_register_1_p16, ram_1_data, register_1_q, register_2_q, register_4_q, sign_extension_1_p3;

  // Inc_Register inc_register_1: pin names not known; wires that end beside it: C8, C7, C6, C5, VARG, VSM, VAQ, VCO, inc_register_1_p9, inc_register_1_p10, inc_register_1_p11, inc_register_1_p12, HCO, inc_register_1_p14, CCO, inc_register_1_p16
  Button RAZ (.out(inc_register_1_p14));
  assign inc_register_1_p9 = VCO ? inc_register_1_p16 : 16'bz;  // Controlled_Buffer controlled_buffer_1
  assign inc_register_1_p9 = VAQ ? register_1_q : 16'bz;  // Controlled_Buffer controlled_buffer_2
  Register #(.width(16)) register_1 (.D(inc_register_1_p12), .Q(register_1_q), .clk(HAQ));  // open: en, clr
  Register #(.width(16)) register_2 (.D(inc_register_1_p12), .Q(register_2_q), .clk(HRADM));  // open: en, clr
  RAM #(.addrWidth(12), .dataWidth(16)) ram_1 (
    .addr(register_2_q[11:0]), .data(ram_1_data), .clk(HEM), .ld(RW));  // open: sel, clr
  assign inc_register_1_p10 = VSM ? controlled_buffer_4_out : 16'bz;  // Controlled_Buffer controlled_buffer_3
  assign controlled_buffer_4_out = not_1_out ? ram_1_data : 16'bz;  // Controlled_Buffer controlled_buffer_4
  not not_1 (not_1_out, not_2_out);
  assign ram_1_data = not_2_out ? inc_register_1_p12 : 16'bz;  // Controlled_Buffer controlled_buffer_5
  not not_2 (not_2_out, RW);
  // ALU alu_1: pin names not known; wires that end beside it: U0, U1, inc_register_1_p9, U2, U3, inc_register_1_p12, inc_register_1_p10, alu_1_p9[1], alu_1_p9[0]
  Register #(.width(2)) register_3 (.D(alu_1_p9), .Q(register_3_q), .clk(HEtat));  // open: en, clr
  Register #(.width(16)) register_4 (.D(inc_register_1_p12), .Q(register_4_q), .clk(HRI));  // open: en, clr
  assign inc_register_1_p10 = VARG ? sign_extension_1_p3 : 16'bz;  // Controlled_Buffer controlled_buffer_6
  // Control_Unit control_unit_1: pin names not known; wires that end beside it: inc_register_1_p12, inc_register_1_p9, register_3_q[0], register_3_q[1], register_4_q[15], control_unit_1_p6, VCO, VAQ, VSM
  // Sign_Extension sign_extension_1: pin names not known; wires that end beside it: register_4_q[11:0], Sext, sign_extension_1_p3, sign_extension_1_p3, inc_register_1_p12, inc_register_1_p11, register_4_q[14], register_4_q[13], register_4_q[12], VARG, C5, C6, C7, C8, Sext, HRI, U0, U1, U2, U3, RW, HEM, HRADM, HAQ, CCO, HCO, HEtat
  Clock Horloge (.out(control_unit_1_p6));

  // Notes on the sheet:
  //   CO
  //   AQ
  //   RADM
  //   SM
  //   EM
  //   Etat
  //   RI in
  //   argument
  //   RI
  //   argument
  //   RI in
  //   A1
  //   A2
  //   R1
  //   R2
endmodule
