// Logisim project ese1010.circ as structural Verilog: 1 circuit, main circuit main
module main (
);

  wire alu_1_p5, alu_1_p9, alu_1_p11, C1, C2, C3, C4, C5, C6, C7, C8, CCO, control_unit_1_p4,
       control_unit_1_p8, HAQ, HCO, HEM, HEtat, HRADM, HRI, inc_register_1_p9, inc_register_1_p10,
       inc_register_1_p11, inc_register_1_p12, inc_register_1_p13, inc_register_1_p16, inc_register_1_p18,
       not_1_out, not_2_out, RW, Sext, U0, U1, U2, U3;
  wire [1:0] alu_1_p14, register_3_q;
  wire [15:0] alu_1_p2, control_unit_1_p1, controlled_buffer_1_out, inc_register_1_p20, inc_register_1_p21,
       inc_register_1_p22, ram_1_data, register_2_q, register_4_q;

  // Inc_Register inc_register_1: pin names not known; wires that end beside it: C8, C7, C6, C5, C4, C3, C2, C1, inc_register_1_p9, inc_register_1_p10, inc_register_1_p11, inc_register_1_p12, inc_register_1_p13, inc_register_1_p11, HCO, inc_register_1_p16, CCO, inc_register_1_p18, inc_register_1_p18, inc_register_1_p20, inc_register_1_p21, inc_register_1_p22
  Button RAZ (.out(inc_register_1_p16));
  Register #(.width(16)) register_1 (.D(inc_register_1_p20), .Q(inc_register_1_p21), .clk(HAQ));  // open: en, clr
  Register #(.width(16)) register_2 (.D(inc_register_1_p22), .Q(register_2_q), .clk(HRADM));  // open: en, clr
  RAM #(.addrWidth(12), .dataWidth(16)) ram_1 (
    .addr(register_2_q[11:0]), .data(ram_1_data), .clk(HEM), .ld(RW));  // open: sel, clr
  assign controlled_buffer_1_out = not_1_out ? ram_1_data : 16'bz;  // Controlled_Buffer controlled_buffer_1
  not not_1 (not_1_out, not_2_out);
  assign ram_1_data = not_2_out ? alu_1_p2 : 16'bz;  // Controlled_Buffer controlled_buffer_2
  not not_2 (not_2_out, RW);
  // ALU alu_1: pin names not known; wires that end beside it: controlled_buffer_1_out, alu_1_p2, U0, U1, alu_1_p5, alu_1_p5, U2, U3, alu_1_p9, alu_1_p9, alu_1_p11, alu_1_p11, alu_1_p14[1], alu_1_p14[0]
  Register #(.width(2)) register_3 (.D(alu_1_p14), .Q(register_3_q), .clk(HEtat));  // open: en, clr
  Register #(.width(16)) register_4 (.D(control_unit_1_p1), .Q(register_4_q), .clk(HRI));  // open: en, clr
  // Control_Unit control_unit_1: pin names not known; wires that end beside it: control_unit_1_p1, inc_register_1_p9, inc_register_1_p10, control_unit_1_p4, register_3_q[0], register_3_q[1], register_4_q[15], control_unit_1_p8, C1, C2, C3
  // Sign_Extension sign_extension_1: pin names not known; wires that end beside it: control_unit_1_p1, register_4_q[11:0], Sext, control_unit_1_p4, control_unit_1_p4, inc_register_1_p13, inc_register_1_p12, register_4_q[14], register_4_q[13], register_4_q[12], C4, C5, C6, C7, C8, Sext, HRI, U3, U2, U1, U0, RW, HEM, HRADM, HAQ, CCO, HCO, HEtat
  Clock Horloge (.out(control_unit_1_p8));

  // Notes on the sheet:
  //   CO
  //   AQ
  //   RADM
  //   SM
  //   EM
  //   Etat
  //   RI in
  //   argument
  //   RI
  //   RI in
  //   argument
  //   A1
  //   A2
  //   R1
  //   R2
endmodule
